# Fritzing sketch Flex (saved by Fritzing 0.9.9b)
breadboards: 1

parts:
  M1 = WeMos D1 Mini V3.1.0
  R3 = Basic Flex Resistor
  R4 = Resistor [tolerance=±5% resistance=1k power=0.25 package=THT]
  C2 = Ceramic Capacitor [capacitance=0.1µF voltage=35V package="100 mil [THT, multilayer]"]

nets:
  N1: M1.D8, R4.Pin_0
  N2: M1.3V3, C2.1
  N3: M1.G, R3.Pin_2
  N4: R3.pin_1, R4.Pin_1, C2.0

custom parts:
  WeMos D1 Mini V3.1.0: The D1 mini is a mini wifi board based on ESP-8266EX.

// code stored in the sketch: Blink.ino
/*
  Blink

  Turns an LED on for one second, then off for one second, repeatedly.
*/

// the setup function runs once when you press reset or power the board
void setup() {
  // initialize digital pin LED_BUILTIN as an output.
  pinMode(LED_BUILTIN, OUTPUT);
}

// the loop function runs over and over again forever
void loop() {
  digitalWrite(LED_BUILTIN, HIGH);   // turn the LED on (HIGH is the voltage level)
  delay(1000);                       // wait for a second
  digitalWrite(LED_BUILTIN, LOW);    // turn the LED off by making the voltage LOW
  delay(1000);                       // wait for a second
}
