# Fritzing sketch HCSR04 (saved by Fritzing 0.9.9b)
breadboards: 1

parts:
  M1 = WeMos D1 Mini V3.1.0
  HC-SR04_Sensor_1 = HC-SR04 Ultrasonic Distance Sensor

nets:
  N1: M1.D7, HC-SR04_Sensor_1.ECHO
  N2: M1.D8, HC-SR04_Sensor_1.TRIG
  3V3: M1.3V3, HC-SR04_Sensor_1.VCC
  N3: M1.G, HC-SR04_Sensor_1.GND

custom parts:
  WeMos D1 Mini V3.1.0: The D1 mini is a mini wifi board based on ESP-8266EX.

// code stored in the sketch: Blink.ino
/*
  Blink

  Turns an LED on for one second, then off for one second, repeatedly.
*/

// the setup function runs once when you press reset or power the board
void setup() {
  // initialize digital pin LED_BUILTIN as an output.
  pinMode(LED_BUILTIN, OUTPUT);
}

// the loop function runs over and over again forever
void loop() {
  digitalWrite(LED_BUILTIN, HIGH);   // turn the LED on (HIGH is the voltage level)
  delay(1000);                       // wait for a second
  digitalWrite(LED_BUILTIN, LOW);    // turn the LED off by making the voltage LOW
  delay(1000);                       // wait for a second
}
