# Fritzing sketch keyboard (saved by Fritzing 0.9.9b)
breadboards: 1

parts:
  M1 = WeMos D1 Mini V3.1.0
  Keypad_TTP224_1x2 = Keypad TTP224 1x4

nets:
  3V3: M1.3V3, Keypad_TTP224_1x2.VCC
  N1: M1.G, Keypad_TTP224_1x2.GND
  N2: M1.D4, Keypad_TTP224_1x2.OUT1
  N3: M1.D3, Keypad_TTP224_1x2.OUT2

custom parts:
  WeMos D1 Mini V3.1.0: The D1 mini is a mini wifi board based on ESP-8266EX.
  Keypad TTP224 1x4: Size: 35 x 29 mm Operating Voltage 2.4 V - 5.5 V Power consumption: 2.5 µA Interfaces: 4x Digital Out Usual high quality and fast delivery directly from Germany by order AZ Delivery Of course, you will receive when you purchase through AZDelivery fully automatically and guarantees a Invoice incl. VAT and according to German Standards Guaranteed ROHS compliance by purchase from the German trader

// code stored in the sketch: Blink.ino
/*
  Blink

  Turns an LED on for one second, then off for one second, repeatedly.
*/

// the setup function runs once when you press reset or power the board
void setup() {
  // initialize digital pin LED_BUILTIN as an output.
  pinMode(LED_BUILTIN, OUTPUT);
}

// the loop function runs over and over again forever
void loop() {
  digitalWrite(LED_BUILTIN, HIGH);   // turn the LED on (HIGH is the voltage level)
  delay(1000);                       // wait for a second
  digitalWrite(LED_BUILTIN, LOW);    // turn the LED off by making the voltage LOW
  delay(1000);                       // wait for a second
}
